# Fritzing sketch LightingRobot (saved by Fritzing 0.9.10b)
stripboards: 6

parts:
  LightingRobot = Arduino Uno (Rev3)
  + = Screw terminal - 2 pins [package=THT]
  5V = Power plug
  GND = Screw terminal - 2 pins [package=THT]
  GND_2 = Screw terminal - 2 pins [package=THT]
  GND_3 = Screw terminal - 2 pins [package=THT]
  +_2 = Screw terminal - 2 pins [package=THT]
  +_3 = Screw terminal - 2 pins [package=THT]
  RoboMaster = Arduino Uno (Rev3)
  U1 = WS2812 RGB LED matrix 8x8
  Mod1 = KY-019 5V Relay Module [package="Breakout board"]
  U2 = WS2812 RGB LED matrix 8x8
  U3 = WS2812 RGB LED matrix 8x8
  Mod3 = KY-019 5V Relay Module [package="Breakout board"]
  Mod4 = KY-019 5V Relay Module [package="Breakout board"]
  Mod5 = KY-019 5V Relay Module [package="Breakout board"]
  Mod6 = KY-019 5V Relay Module [package="Breakout board"]
  GND1 = Screw terminal - 2 pins [package=THT]
  GND2 = Screw terminal - 2 pins [package=THT]
  GND3 = Screw terminal - 2 pins [package=THT]
  GND4 = Screw terminal - 2 pins [package=THT]
  GND5 = Screw terminal - 2 pins [package=THT]
  GND6 = Screw terminal - 2 pins [package=THT]
  +1 = Screw terminal - 2 pins [package=THT]
  5V1 = Power plug
  +2 = Screw terminal - 2 pins [package=THT]
  +3 = Screw terminal - 2 pins [package=THT]
  GND7 = Screw terminal - 2 pins [package=THT]
  GND8 = Screw terminal - 2 pins [package=THT]
  GND9 = Screw terminal - 2 pins [package=THT]
  LED1 = LED - 5mm [color="Red (633nm)" current=0.030 package="5 mm [THT]"]
  Mod2 = KY-019 5V Relay Module [package="Breakout board"]
  LED2 = LED - 5mm [color="Red (633nm)" current=0.030 package="5 mm [THT]"]
  LED3 = LED - 5mm [color="Red (633nm)" current=0.030 package="5 mm [THT]"]
  LED4 = LED - 5mm [color="Red (633nm)" current=0.030 package="5 mm [THT]"]
  LED5 = LED - 5mm [color="Red (633nm)" current=0.030 package="5 mm [THT]"]
  LED6 = LED - 5mm [color="Red (633nm)" current=0.030 package="5 mm [THT]"]

nets:
  N1: LightingRobot.A4/SDA, RoboMaster.A4/SDA
  N2: LightingRobot.A5/SCL, RoboMaster.A5/SCL
  N3: LightingRobot.D9_PWM, U1.DIN
  GND: LightingRobot.GND, 5V.GND, GND.pin1, GND.pin2, GND_2.pin1, GND_2.pin2, GND_3.pin1, GND_3.pin2, RoboMaster.GND, U1.GND#0, Mod1.-, Mod3.-, Mod4.-, Mod5.-, Mod6.-, GND4.pin1, GND4.pin2, GND5.pin1, GND5.pin2, GND6.pin1, GND6.pin2, Mod2.-
  N4: LightingRobot.D2, Mod6.S
  N5: LightingRobot.D3_PWM, Mod5.S
  N6: LightingRobot.D4, Mod4.S
  N7: LightingRobot.D5_PWM, Mod3.S
  N8: LightingRobot.D6_PWM, Mod2.S
  N9: LightingRobot.D7, Mod1.S
  N10: LightingRobot.5V, Mod1.+, Mod3.+, Mod4.+, Mod5.+, Mod6.+, GND1.pin1, GND1.pin2, GND2.pin1, GND2.pin2, GND3.pin1, GND3.pin2, Mod2.+
  VCC: +.pin1, +.pin2, 5V.VCC, +_2.pin1, +_2.pin2, +_3.pin1, +_3.pin2, U1.VCC, U2.VCC, U3.VCC
  N11: U1.GND#4, U2.GND#0
  N12: U1.DOUT, U2.DIN
  N13: Mod1.Common, LED6.cathode
  N14: Mod1.NO, Mod3.NO, Mod4.NO, Mod5.NO, Mod6.NO, 5V1.GND, GND7.pin1, GND7.pin2, GND8.pin1, GND8.pin2, GND9.pin1, GND9.pin2, Mod2.NO
  N15: U2.GND#4, U3.GND
  N16: U2.DOUT, U3.DIN
  N17: Mod3.Common, LED4.cathode
  N18: Mod4.Common, LED3.cathode
  N19: Mod5.Common, LED2.cathode
  N20: Mod6.Common, LED1.cathode
  N21: +1.pin1, +1.pin2, 5V1.VCC, +2.pin1, +2.pin2, +3.pin1, +3.pin2, LED1.anode, LED2.anode, LED3.anode, LED4.anode, LED5.anode, LED6.anode
  N22: Mod2.Common, LED5.cathode

notes:
  RoboMaster
  5V
  LightingRobot

custom parts:
  WS2812 RGB LED matrix 8x8: WS2812 matrix 8x8
  KY-019 5V Relay Module: KY-019 5V Relay module, used to control AC circuits. (Special thanks to vanepp for fixing the PCB holes and other errors)
